# Fritzing sketch FlashFlood-Forecaster (saved by Fritzing 0.9.3b)
breadboards: 1

parts:
  MH-ET_LIVE_ESP32_DEVKIT1 = MH-ET LIVE ESP32 DEVKIT 38 pins
  DHT2 = DHT11 Humitidy and Temperature Sensor (3 pins)
  Part1 = Adafruit BMP180
  YL-83_-_Detection_Board1 = YL-83 Rain Sensor - Detection Board
  YL-83_-_Control_Board1 = YL-83 Rain Sensor - Control Board
  J1 = Piezo Speaker
  LED1 = smd LED [color="Red (633nm)" package="0603 [SMD]"]
  Part2 = Solar Panel [package="Renogy 50 Watts 12 Volt Monocrystalline Bendable Solar Panel"]
  U1 = LM2596 step down module
  BAT1 = 18650 battery holder [package=battery-18650-kit]
  Part3 = LCD1602-I2C

nets:
  3V3: MH-ET_LIVE_ESP32_DEVKIT1.3V3, Part1.+3V3
  N1: MH-ET_LIVE_ESP32_DEVKIT1.IO34, YL-83_-_Control_Board1.AO
  N2: MH-ET_LIVE_ESP32_DEVKIT1.IO26, J1.pin2
  N3: MH-ET_LIVE_ESP32_DEVKIT1.IO14, LED1.anode
  N4: MH-ET_LIVE_ESP32_DEVKIT1.IO13, DHT2.Signal
  VCC: MH-ET_LIVE_ESP32_DEVKIT1.5V, DHT2.Plus, YL-83_-_Control_Board1.VCC, Part3.VCC
  GND: MH-ET_LIVE_ESP32_DEVKIT1.GND, Part1.GND, YL-83_-_Control_Board1.GND, J1.pin1, LED1.cathode, Part3.GND
  N5: MH-ET_LIVE_ESP32_DEVKIT1.IO22, Part1.SCL, Part3.SCL
  N6: MH-ET_LIVE_ESP32_DEVKIT1.IO21, Part1.SDA, Part3.SDA
  N7: YL-83_-_Detection_Board1.POS, YL-83_-_Control_Board1.POS
  N8: YL-83_-_Detection_Board1.NEG, YL-83_-_Control_Board1.NEG
  N9: Part2.Connector_1, U1.IN+
  N10: Part2.Connector_2, U1.IN-, U1.OUT-, BAT1.-
  N11: U1.OUT+, BAT1.+

custom parts:
  MH-ET LIVE ESP32 DEVKIT 38 pins: http://mh.nodebb.com/topic/2/mh-et-live-esp32-devkit
  DHT11 Humitidy and Temperature Sensor (3 pins): DHT11 Humidity and Temperature Sensor (3 pins).
  Adafruit BMP180: This precision sensor from Bosch is the best low-cost sensing solution for measuring barometric pressure and temperature. Because pressure changes with altitude you can also use it as an altimeter! The sensor is soldered onto a PCB with a 3.3V regulator, I2C level shifter and pull-up resistors on the I2C pins. The BMP180 is the next-generation of sensors from Bosch, and replaces the BMP085.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
  YL-83 Rain Sensor - Detection Board: The YL-83 is a rain sensor that has more resistance when dry and less resistance when wet. The module runs at 5V.
  YL-83 Rain Sensor - Control Board: The YL-83 is a rain sensor that has more resistance when dry and less resistance when wet. The module runs at 5V.
  Solar Panel: Renogy 50 Watts 12 Volt Solar Panel
  LM2596 step down module: LM2596 DC-DC step down power supply module 3 A.
  18650 battery holder: 18650 Battery Holder
  LCD1602-I2C: A standard character display, usually with 2x16 characters. Comes in many colors with LCM1602 IIC attached.
